// Logisim project gabriel.circ as structural Verilog: 4 circuits, main circuit celula
module celula (
  input  direita,
  input  esquerda,
  input  A,
  input  B,
  input  vem_1,
  input  [2:0] Controlador,
  output S,
  output vai_1
);

  wire and_1_out, and_2_out, nand_1_out, or_1_out, somador_1_s, somador_1_vai_1, subtrador_1_s,
       subtrador_1_vai_1, xor_1_out;

  and and_1 (and_1_out, A, B);
  or or_1 (or_1_out, A, B);
  nand nand_1 (nand_1_out, A, B);
  xor xor_1 (xor_1_out, A, B);
  somador somador_1 (.A(A), .B(B), .Vem_1(vem_1), .S(somador_1_s), .Vai_1(somador_1_vai_1));
  subtrador subtrador_1 (.A(A), .B(B), .vem_1(vem_1), .S(subtrador_1_s), .Vai_1(subtrador_1_vai_1));
  and and_2 (and_2_out, Controlador[2], ~Controlador[1], Controlador[0]);  // AND_Gate
  Multiplexer #(.enable("false")) multiplexer_1 (
    .in0(somador_1_vai_1), .in1(subtrador_1_vai_1), .out(vai_1), .sel(and_2_out));
  Multiplexer #(.select(3), .enable("false")) multiplexer_2 (
    .in0(and_1_out), .in1(or_1_out), .in2(nand_1_out), .in3(xor_1_out), .in4(somador_1_s),
    .in5(subtrador_1_s), .in6(direita), .in7(esquerda), .out(S), .sel(Controlador));
endmodule

module somador (
  input  A,
  input  B,
  input  Vem_1,
  output S,
  output Vai_1
);

  wire and_1_out, and_2_out, and_3_out, xor_1_out;

  xor xor_1 (xor_1_out, A, B);
  and and_1 (and_1_out, B, Vem_1);
  and and_2 (and_2_out, A, Vem_1);
  and and_3 (and_3_out, A, B);
  xor xor_2 (S, xor_1_out, Vem_1);
  or or_1 (Vai_1, and_1_out, and_2_out, and_3_out);
endmodule

module subtrador (
  input  A,
  input  B,
  input  vem_1,
  output S,
  output Vai_1
);

  wire and_1_out, and_2_out, and_3_out, xor_1_out;

  and and_1 (and_1_out, ~A, vem_1);  // AND_Gate
  and and_2 (and_2_out, ~A, B);  // AND_Gate
  and and_3 (and_3_out, B, vem_1);
  xor xor_1 (xor_1_out, A, B);
  xor xor_2 (S, xor_1_out, vem_1);
  or or_1 (Vai_1, and_1_out, and_2_out, and_3_out);
endmodule

// Overflow
module ula (
  input  [3:0] A,
  input  [2:0] Controle,
  input  [3:0] B,
  output Overflow,
  output [3:0] S
);

  wire celula_2_vai_1, celula_3_vai_1, celula_4_vai_1;

  celula celula_1 (
    .esquerda(A[2]), .A(A[3]), .B(B[3]), .vem_1(celula_2_vai_1), .Controlador(Controle), .direita(1'b0),
    .S(S[3]), .vai_1(Overflow));
  celula celula_2 (
    .esquerda(A[1]), .A(A[2]), .B(B[2]), .vem_1(celula_3_vai_1), .Controlador(Controle), .direita(A[3]),
    .S(S[2]), .vai_1(celula_2_vai_1));
  celula celula_3 (
    .esquerda(A[0]), .A(A[1]), .B(B[1]), .vem_1(celula_4_vai_1), .Controlador(Controle), .direita(A[2]),
    .S(S[1]), .vai_1(celula_3_vai_1));
  celula celula_4 (
    .esquerda(1'b0), .A(A[0]), .B(B[0]), .vem_1(1'b0), .Controlador(Controle), .direita(A[1]), .S(S[0]),
    .vai_1(celula_4_vai_1));

  // Notes on the sheet:
  //   0000 - AND
  //   0001 - OR
  //   0010 - NAND
  //   0011 - XOR
  //   0100 - SOMA
  //   0101 - SUBTRAÇAO
  //   0110 - Deslocamento DIR
  //   0111 - Deslocamento ESQ
endmodule
